// Logisim project FcontrolUnit.circ as structural Verilog: 1 circuit, main circuit main
module main (
  input  [3:0] in_1,
  output ALUsrc,
  output ALUop,
  output memRead,
  output memWrite,
  output RegWrite,
  output memToReg,
  output RegDst,
  output Branch,
  output Jump
);

  wire nand_1_out, nand_2_out, nand_3_out, nand_4_out, nand_5_out, nand_6_out, nand_7_out, nand_8_out,
       nand_9_out, nand_10_out, nand_11_out, nand_12_out, nand_13_out, nand_14_out, nand_15_out, nand_16_out,
       nand_17_out, nand_18_out, nand_19_out, nand_20_out, nand_21_out, nand_22_out, nand_23_out,
       nand_24_out, nand_25_out, nand_26_out, nand_27_out, nand_28_out, nand_29_out, nand_30_out,
       nand_31_out, nand_32_out, nand_33_out, nand_34_out, nand_35_out, nand_36_out, nand_37_out,
       nand_38_out, nand_39_out, nand_40_out, nand_41_out, nand_42_out, nand_43_out, nand_44_out,
       nand_45_out, nand_46_out, nand_47_out, nand_48_out, nand_49_out;

  nand nand_1 (nand_1_out, in_1[1], in_1[1]);
  nand nand_2 (nand_2_out, in_1[3], in_1[3]);
  nand nand_3 (nand_3_out, in_1[2], in_1[2]);
  nand nand_4 (nand_4_out, in_1[3], in_1[3]);
  nand nand_5 (nand_5_out, in_1[1], in_1[1]);
  nand nand_6 (nand_6_out, in_1[3], in_1[3]);
  nand nand_7 (nand_7_out, in_1[0], in_1[0]);
  nand nand_8 (nand_8_out, in_1[2], in_1[2]);
  nand nand_9 (nand_9_out, in_1[1], in_1[1]);
  nand nand_10 (nand_10_out, in_1[0], in_1[0]);
  nand nand_11 (nand_11_out, in_1[2], in_1[2]);
  nand nand_12 (nand_12_out, in_1[1], in_1[1]);
  nand nand_13 (nand_13_out, in_1[2], in_1[2]);
  nand nand_14 (nand_14_out, in_1[1], in_1[1]);
  nand nand_15 (nand_15_out, in_1[3], in_1[3]);
  nand nand_16 (nand_16_out, in_1[2], in_1[2]);
  nand nand_17 (nand_17_out, in_1[3], in_1[3]);
  nand nand_18 (nand_18_out, in_1[0], in_1[0]);
  nand nand_19 (nand_19_out, in_1[1], in_1[1]);
  nand nand_20 (nand_20_out, in_1[0], in_1[0]);
  nand nand_21 (nand_21_out, in_1[1], in_1[1]);
  nand nand_22 (nand_22_out, in_1[2], in_1[2]);
  nand nand_23 (nand_23_out, in_1[1], in_1[1]);
  nand nand_24 (nand_24_out, in_1[3], in_1[3]);
  nand nand_25 (nand_25_out, in_1[2], in_1[2]);
  nand nand_26 (nand_26_out, in_1[3], in_1[3]);
  nand nand_27 (nand_27_out, in_1[0], in_1[0]);
  nand nand_28 (nand_28_out, in_1[1], in_1[1]);
  nand nand_29 (nand_29_out, in_1[0], in_1[0]);
  nand nand_30 (nand_30_out, in_1[3], in_1[2], in_1[1], in_1[0]);
  nand nand_31 (nand_31_out, in_1[3], in_1[2], in_1[1], in_1[0]);
  nand nand_32 (nand_32_out, in_1[3], nand_1_out);
  nand nand_33 (nand_33_out, in_1[3], in_1[2], in_1[0]);
  nand nand_34 (nand_34_out, nand_2_out, nand_3_out);
  nand nand_35 (nand_35_out, nand_4_out, nand_5_out);
  nand nand_36 (nand_36_out, nand_6_out, nand_7_out);
  nand nand_37 (nand_37_out, in_1[3], nand_8_out, nand_9_out, nand_10_out);
  nand nand_38 (nand_38_out, in_1[3], in_1[2], in_1[1], in_1[0]);
  nand nand_39 (nand_39_out, in_1[3], nand_11_out, nand_12_out, in_1[0]);
  nand nand_40 (nand_40_out, in_1[3], nand_13_out, nand_14_out, in_1[0]);
  nand nand_41 (nand_41_out, nand_15_out, nand_16_out);
  nand nand_42 (nand_42_out, nand_17_out, nand_18_out);
  nand nand_43 (nand_43_out, nand_19_out, nand_20_out);
  nand nand_44 (nand_44_out, in_1[2], nand_21_out);
  nand nand_45 (nand_45_out, in_1[3], nand_22_out, nand_23_out);
  nand nand_46 (nand_46_out, nand_24_out, nand_25_out);
  nand nand_47 (nand_47_out, nand_26_out, nand_27_out);
  nand nand_48 (nand_48_out, in_1[2], nand_28_out);
  nand nand_49 (nand_49_out, in_1[3], in_1[2], in_1[1], nand_29_out);
  nand nand_50 (Jump, nand_30_out, nand_31_out);
  nand nand_51 (ALUsrc, nand_32_out, nand_33_out);
  nand nand_52 (ALUop, nand_34_out, nand_35_out, nand_36_out);
  nand nand_53 (memRead, nand_37_out, nand_38_out);
  nand nand_54 (memWrite, nand_39_out, nand_40_out);
  nand nand_55 (RegWrite, nand_41_out, nand_42_out, nand_43_out, nand_44_out);
  nand nand_56 (memToReg, nand_45_out, nand_45_out);
  nand nand_57 (RegDst, nand_46_out, nand_47_out, nand_48_out);
  nand nand_58 (Branch, nand_49_out, nand_49_out);
endmodule
