// Logisim project alu control.circ as structural Verilog: 1 circuit, main circuit main
// ALUcontrol
module main (
  input  ALUop,
  input  I3,
  input  I2,
  input  I1,
  input  I0,
  output O2,
  output O1,
  output O0,
  output Enable
);

  wire nand_1_out, nand_2_out, nand_3_out, nand_4_out, nand_5_out, nand_6_out, nand_7_out, nand_9_out,
       nand_10_out, nand_11_out, nand_12_out, nand_13_out;

  nand nand_1 (nand_1_out, I2, I2);
  nand nand_2 (nand_2_out, I3, I3);
  nand nand_3 (nand_3_out, I3, I3);
  nand nand_4 (nand_4_out, I3, I3);
  nand nand_5 (nand_5_out, I2, I2);
  nand nand_6 (nand_6_out, I1, I1);
  nand nand_7 (nand_7_out, I0, I0);
  nand nand_8 (O2, nand_1_out, nand_2_out);
  nand nand_9 (nand_9_out, nand_3_out, I0);
  nand nand_10 (nand_10_out, I2, I0);
  nand nand_11 (nand_11_out, ALUop, nand_4_out, nand_5_out);
  nand nand_12 (nand_12_out, ALUop, nand_6_out);
  nand nand_13 (nand_13_out, ALUop, I2, nand_7_out);
  nand nand_14 (O0, nand_9_out, nand_10_out);
  nand nand_15 (Enable, nand_11_out, nand_12_out, nand_13_out);

  assign O1 = I1;
endmodule
