// Logisim project mainCont.circ as structural Verilog: 1 circuit, main circuit main
module main (
  input  [3:0] in_1,
  output ALUsrc,
  output ALUop,
  output MenRead,
  output MemWrite,
  output RegWrite,
  output MemToReg,
  output Branch,
  output RegDst,
  output Jump
);

  wire nand_1_out, nand_2_out, nand_3_out, nand_4_out, nand_5_out, nand_6_out, nand_7_out, nand_8_out,
       nand_9_out, nand_10_out, nand_11_out, nand_12_out, nand_13_out, nand_14_out, nand_15_out, nand_16_out,
       nand_17_out, nand_18_out, nand_19_out, nand_20_out, nand_21_out, nand_22_out, nand_23_out,
       nand_24_out, nand_25_out, nand_26_out, nand_27_out, nand_28_out, nand_29_out, nand_30_out,
       nand_31_out, nand_32_out, nand_33_out, nand_34_out, nand_35_out, nand_36_out, nand_37_out,
       nand_38_out, nand_39_out, nand_40_out, nand_41_out, nand_42_out, nand_43_out, nand_44_out,
       nand_45_out, nand_46_out, nand_49_out, nand_50_out, nand_52_out;

  nand nand_1 (nand_1_out, in_1[1], in_1[1]);
  nand nand_2 (nand_2_out, in_1[0], in_1[0]);
  nand nand_3 (nand_3_out, in_1[3], in_1[3]);
  nand nand_4 (nand_4_out, in_1[2], in_1[2]);
  nand nand_5 (nand_5_out, in_1[3], in_1[3]);
  nand nand_6 (nand_6_out, in_1[1], in_1[1]);
  nand nand_7 (nand_7_out, in_1[3], in_1[3]);
  nand nand_8 (nand_8_out, in_1[0], in_1[0]);
  nand nand_9 (nand_9_out, in_1[2], in_1[2]);
  nand nand_10 (nand_10_out, in_1[1], in_1[1]);
  nand nand_11 (nand_11_out, in_1[0], in_1[0]);
  nand nand_12 (nand_12_out, in_1[2], in_1[2]);
  nand nand_13 (nand_13_out, in_1[1], in_1[1]);
  nand nand_14 (nand_14_out, in_1[3], in_1[3]);
  nand nand_15 (nand_15_out, in_1[2], in_1[2]);
  nand nand_16 (nand_16_out, in_1[3], in_1[3]);
  nand nand_17 (nand_17_out, in_1[0], in_1[0]);
  nand nand_18 (nand_18_out, in_1[1], in_1[1]);
  nand nand_19 (nand_19_out, in_1[0], in_1[0]);
  nand nand_20 (nand_20_out, in_1[1], in_1[1]);
  nand nand_21 (nand_21_out, in_1[2], in_1[2]);
  nand nand_22 (nand_22_out, in_1[1], in_1[1]);
  nand nand_23 (nand_23_out, in_1[0], in_1[0]);
  nand nand_24 (nand_24_out, in_1[3], in_1[3]);
  nand nand_25 (nand_25_out, in_1[2], in_1[2]);
  nand nand_26 (nand_26_out, in_1[3], in_1[3]);
  nand nand_27 (nand_27_out, in_1[1], in_1[1]);
  nand nand_28 (nand_28_out, in_1[3], in_1[3]);
  nand nand_29 (nand_29_out, in_1[0], in_1[0]);
  nand nand_30 (nand_30_out, in_1[3], in_1[2], in_1[1], in_1[0]);
  nand nand_31 (nand_31_out, in_1[3], nand_1_out, nand_2_out);
  nand nand_32 (nand_32_out, in_1[3], in_1[2], in_1[0]);
  nand nand_33 (nand_33_out, nand_3_out, nand_4_out);
  nand nand_34 (nand_34_out, nand_5_out, nand_6_out);
  nand nand_35 (nand_35_out, nand_7_out, nand_8_out);
  nand nand_36 (nand_36_out, in_1[3], in_1[2], in_1[1], in_1[0]);
  nand nand_37 (nand_37_out, nand_14_out, nand_15_out);
  nand nand_38 (nand_38_out, nand_16_out, nand_17_out);
  nand nand_39 (nand_39_out, nand_18_out, nand_19_out);
  nand nand_40 (nand_40_out, in_1[2], nand_20_out);
  nand nand_41 (nand_41_out, in_1[3], nand_21_out, nand_22_out);
  nand nand_42 (nand_42_out, in_1[3], in_1[2], in_1[1], in_1[0]);
  nand nand_43 (nand_43_out, nand_24_out, nand_25_out);
  nand nand_44 (nand_44_out, nand_26_out, nand_27_out);
  nand nand_45 (nand_45_out, nand_28_out, nand_29_out);
  nand nand_46 (nand_46_out, in_1[3], in_1[2]);
  nand nand_47 (Jump, nand_30_out, nand_30_out);
  nand nand_48 (ALUsrc, nand_31_out, nand_32_out);
  nand nand_49 (nand_49_out, in_1[3], nand_9_out, nand_10_out, nand_11_out);
  nand nand_50 (nand_50_out, in_1[3], nand_12_out, nand_13_out, in_1[0]);
  nand nand_51 (MemToReg, nand_41_out, nand_42_out);
  nand nand_52 (nand_52_out, in_1[3], in_1[2], in_1[1], nand_23_out);
  nand nand_53 (ALUop, nand_33_out, nand_34_out, nand_35_out, nand_36_out);
  nand nand_54 (MenRead, nand_49_out, nand_49_out);
  nand nand_55 (MemWrite, nand_50_out, nand_50_out);
  nand nand_56 (RegWrite, nand_37_out, nand_38_out, nand_39_out, nand_40_out);
  nand nand_57 (Branch, nand_52_out, nand_52_out);
  nand nand_58 (RegDst, nand_43_out, nand_44_out, nand_45_out, nand_46_out);
endmodule
